// Logisim project MULTIPLEXER.circ as structural Verilog: 1 circuit, main circuit main
module main (
  input  in_1,
  input  in_2,
  input  in_3,
  input  in_4,
  input  in_5,
  input  in_6,
  input  in_7,
  input  in_8,
  input  in_9,
  input  in_10,
  input  in_11,
  input  in_12,
  input  in_13,
  input  in_14,
  input  in_15,
  input  in_16,
  input  in_17,
  input  in_18,
  input  in_19,
  input  in_20,
  output out_21
);

  wire and_1_out, and_2_out, and_3_out, and_4_out, and_5_out, and_6_out, and_7_out, and_8_out, and_9_out,
       and_10_out, and_11_out, and_12_out, and_13_out, and_14_out, and_15_out, and_16_out, and_17_out,
       and_18_out, and_19_out, and_20_out, not_1_out, not_2_out, not_3_out, not_4_out, or_1_out, or_2_out,
       or_3_out, or_4_out;

  not not_1 (not_1_out, in_1);
  not not_2 (not_2_out, in_2);
  and and_1 (and_1_out, in_3, not_2_out, not_1_out);
  and and_2 (and_2_out, in_4, in_2, in_1);
  and and_3 (and_3_out, in_5, not_2_out, in_1);
  and and_4 (and_4_out, in_6, in_2, not_1_out);
  and and_5 (and_5_out, in_7, not_2_out, not_1_out);
  and and_6 (and_6_out, in_8, in_2, in_1);
  and and_7 (and_7_out, in_11, not_2_out, in_1);
  and and_8 (and_8_out, in_12, in_2, not_1_out);
  and and_9 (and_9_out, in_13, not_2_out, not_1_out);
  and and_10 (and_10_out, in_14, in_2, in_1);
  and and_11 (and_11_out, in_15, not_2_out, in_1);
  and and_12 (and_12_out, in_16, in_2, not_1_out);
  and and_13 (and_13_out, in_17, not_2_out, not_1_out);
  and and_14 (and_14_out, in_18, in_2, in_1);
  and and_15 (and_15_out, in_19, not_2_out, in_1);
  and and_16 (and_16_out, in_20, in_2, not_1_out);
  or or_1 (or_1_out, and_1_out, and_2_out, and_3_out, and_4_out);
  or or_2 (or_2_out, and_5_out, and_6_out, and_7_out, and_8_out);
  or or_3 (or_3_out, and_9_out, and_10_out, and_11_out, and_12_out);
  or or_4 (or_4_out, and_13_out, and_14_out, and_15_out, and_16_out);
  not not_3 (not_3_out, in_9);
  not not_4 (not_4_out, in_10);
  and and_17 (and_17_out, or_1_out, not_4_out, not_3_out);
  and and_18 (and_18_out, or_2_out, in_10, in_9);
  and and_19 (and_19_out, or_3_out, not_4_out, in_9);
  and and_20 (and_20_out, or_4_out, in_10, not_3_out);
  or or_5 (out_21, and_17_out, and_18_out, and_19_out, and_20_out);
endmodule
